# Fritzing sketch Solenoides (saved by Fritzing 0.7.12b)
breadboards: 1

parts:
  ULN2803 = IC, DIP package, 18 pins [chip_label=IC]
  Arduino_Uno = Arduino
  Fonte = Screw terminal - 2 pins [package=THT]
  Solenóides = screw terminal, 9 pins

nets:
  N1: ULN2803.pin1, Arduino_Uno.D2
  N2: ULN2803.pin2, Arduino_Uno.D3
  N3: ULN2803.pin3, Arduino_Uno.D4
  N4: ULN2803.pin4, Arduino_Uno.D5
  N5: ULN2803.pin5, Arduino_Uno.D6
  N6: ULN2803.pin6, Arduino_Uno.D7
  N7: ULN2803.pin7, Arduino_Uno.D8
  N8: ULN2803.pin8, Arduino_Uno.D9
  N9: ULN2803.pin9, Arduino_Uno.GND, Fonte.pin2
  N10: ULN2803.pin10, Fonte.pin1, Solenóides.pin9
  N11: ULN2803.pin11, Solenóides.pin8
  N12: ULN2803.pin12, Solenóides.pin7
  N13: ULN2803.pin13, Solenóides.pin6
  N14: ULN2803.pin14, Solenóides.pin5
  N15: ULN2803.pin15, Solenóides.pin4
  N16: ULN2803.pin16, Solenóides.pin3
  N17: ULN2803.pin17, Solenóides.pin2
  N18: ULN2803.pin18, Solenóides.pin1
